# Fritzing sketch FireLampV1r3 (saved by Fritzing 0.9.2b)
circuit board: 5.34521cm x 5.52784cm
breadboards: 2

parts:
  L1 = female pin header, 4 pins [form="♀ (female)"]
  L2 = female pin header, 4 pins [form="♀ (female)"]
  L3 = female pin header, 4 pins [form="♀ (female)"]
  L4 = female pin header, 4 pins [form="♀ (female)"]
  LED60 = female pin header, 3 pins [form="♀ (female)"]
  LED24 = female pin header, 3 pins [form="♀ (female)"]
  LED16 = female pin header, 3 pins [form="♀ (female)"]
  POT1 = female pin header, 3 pins [form="♀ (female)"]
  POT2 = female pin header, 3 pins [form="♀ (female)"]
  I2C1 = female pin header, 4 pins [form="♀ (female)"]
  I2C2 = female pin header, 4 pins [form="♀ (female)"]
  DHT = female pin header, 3 pins [form="♀ (female)"]
  B1 = female pin header, 2 pins [form="♀ (female)"]
  Parte1 = Arduino Uno (Rev3)
  Power_selecct = male pin header, 3 pins [form="♂ (male)"]
  POT3 = female pin header, 3 pins [form="♀ (female)"]

nets:
  N1: L1.pin1, L1.pin4, L2.pin1, L2.pin4, L3.pin1, L3.pin4, L4.pin1, L4.pin4, LED60.pin1, LED24.pin1, LED16.pin1, POT1.pin3, POT2.pin3, I2C1.pin4, I2C2.pin4, DHT.pin1, B1.pin1, Parte1.GND, POT3.pin3
  N2: L1.pin2, L2.pin2, L3.pin2, L4.pin2, Power_selecct.pin2
  N3: L1.pin3, Parte1.D12/MISO
  N4: L2.pin3, Parte1.D11_PWM/MOSI
  N5: L3.pin3, Parte1.D10_PWM/SS
  N6: L4.pin3, Parte1.D9_PWM
  N7: LED60.pin2, Parte1.D5_PWM
  N8: LED60.pin3, LED24.pin3, LED16.pin3
  N9: LED24.pin2, Parte1.D4
  N10: LED16.pin2, Parte1.D3_PWM
  N11: POT1.pin1, POT2.pin1, I2C1.pin1, I2C2.pin1, DHT.pin3, Parte1.5V, Power_selecct.pin1, POT3.pin1
  N12: POT1.pin2, Parte1.A0
  N13: POT2.pin2, Parte1.A1
  N14: I2C1.pin2, I2C2.pin2, Parte1.A4/SDA
  N15: I2C1.pin3, I2C2.pin3, Parte1.A5/SCL
  N16: DHT.pin2, Parte1.D8
  N17: B1.pin2, Parte1.D13/SCK
  N18: Parte1.A2, POT3.pin2
  N19: Parte1.VIN, Power_selecct.pin3

notes:
  LedFire v1 r3
  2018 Samuel Villafranca
  5V
  VIN
